// Logisim project Piplined.circ as structural Verilog: 14 circuits, main circuit Data_Path
module Data_Path (
  output [2:0] out_1,
  output [2:0] out_2,
  output [2:0] out_3
);

  wire AluSrc, and_1_out, and_2_out, Branch, clk, inverseA, inverseB, Jump, JumpSrc, kill1, lessThan, Lui2,
       Lui3, Lui4, Mem_read_alu, MemRead, MemToReg, MemWrite, not_1_out, not_2_out, OverFlow, RegWr_ALU,
       RegWr_MEM, RegWr_WB, stall, zero;
  wire [1:0] forward_A, forward_B, new_control_unit_1_writedatasrc, RegsDst, writeDataSrc;
  wire [2:0] Funct, multiplexer_1_out, Rd_ALU, Rd_MEM, Rd_WB;
  wire [3:0] aluOp, id_ex_1_op_out, Op;
  wire [5:0] alu_ctrl_unit_1_aluop;
  wire [6:0] ex_mem_1_control_signals_2, id_ex_1_control_signals_2, new_control_unit_1_regwr;
  wire [11:0] adder_1_out, adder_2_out, bit_extender_2_out, id_ex_1_bta_out, multiplexer_2_out,
       multiplexer_5_out, multiplexer_7_out, NPC, register_1_q;
  wire [15:0] A, Alu_res, B, bit_extender_1_out, bit_extender_3_out, bit_extender_4_out,
       ex_mem_1_alu_result_2, ex_mem_1_data_to_mem_2, ex_mem_1_npc_2, id_ex_1_imm_2, id_ex_1_npc_2,
       id_ex_1_rs_2, id_ex_1_rt_2, lui_data_alu, lui_data_MEM, lui_data_WB, Mem_res, mem_wb_1_mem_data_out_2,
       multiplexer_6_out, multiplexer_10_out, ram_1_data, register_file_1_read_data_1,
       register_file_1_read_data_2, rom_1_data, shifter_1_out, WD, Write_Back;
  wire [15:1] alu_1_result;

  not not_1 (not_1_out, stall);
  Register #(.width(12)) register_1 (.D(multiplexer_7_out), .en(not_1_out), .Q(register_1_q), .clk(clk));  // open: clr
  not not_2 (not_2_out, Branch);
  Clock clock_1 (.out(clk));
  and and_1 (and_1_out, not_2_out, Jump);
  Adder #(.width(12)) adder_1 (.a(12'h1), .b(register_1_q), .out(adder_1_out));  // open: cin, cout
  ROM #(.addrWidth(12), .dataWidth(16)) rom_1 (.addr(register_1_q), .data(rom_1_data), .sel(1'b1));
  or or_1 (kill1, Branch, and_1_out);
  IF_ID if_id_1 (
    .NPC(adder_1_out), .instruction_in(rom_1_data), .clk(clk), .NPC_2(NPC),
    .instruction_out({Op, out_1, out_2, out_3, Funct}), .kill1(kill1), .stall(stall));
  assign bit_extender_1_out = {{4{1'b0}}, {out_1, out_2, out_3, Funct}};  // Bit_Extender bit_extender_1
  Shifter #(.width(16)) shifter_1 (.in(bit_extender_1_out), .\dist (4'b0100), .out(shifter_1_out));
  ALU_CTRL_Unit alu_ctrl_unit_1 (
    .Op(Op), .func(Funct), .aluop(alu_ctrl_unit_1_aluop[3:0]), .inversA(alu_ctrl_unit_1_aluop[4]),
    .inversB(alu_ctrl_unit_1_aluop[5]));
  new_control_unit new_control_unit_1 (
    .op(Op), .Func(Funct), .RegWr(new_control_unit_1_regwr[0]), .Alurc(new_control_unit_1_regwr[1]),
    .MemWrite(new_control_unit_1_regwr[2]), .MemRead(new_control_unit_1_regwr[3]), .Jump(Jump),
    .Jump_Src(JumpSrc), .RegDst(RegsDst), .writeDataSrc(new_control_unit_1_writedatasrc),
    .MemToReg(new_control_unit_1_regwr[6]));
  assign bit_extender_2_out = {{6{out_3[2]}}, {out_3, Funct}};  // Bit_Extender bit_extender_2
  Adder #(.width(12)) adder_2 (.a(NPC), .b(bit_extender_2_out), .out(adder_2_out));  // open: cin, cout
  Multiplexer #(.select(2), .width(3), .enable("false")) multiplexer_1 (
    .in0(out_2), .in1(out_3), .in2(3'b111), .in3(3'b001), .out(multiplexer_1_out), .sel(RegsDst));
  assign bit_extender_3_out = {{4{1'b0}}, NPC};  // Bit_Extender bit_extender_3
  assign bit_extender_4_out = {{10{out_3[2]}}, {out_3, Funct}};  // Bit_Extender bit_extender_4
  and and_2 (and_2_out, RegsDst[0], RegsDst[1]);
  Multiplexer #(.width(12), .enable("false")) multiplexer_2 (
    .in0({out_1, out_2, out_3, Funct}), .in1(A[11:0]), .out(multiplexer_2_out), .sel(JumpSrc));
  Register_File register_file_1 (
    .Write_register(Rd_WB), .Write_Data(WD), .Read_Data_1(register_file_1_read_data_1),
    .Read_Data_2(register_file_1_read_data_2), .RegWrite(RegWr_WB), .read_register_1(out_1),
    .read_register_2(out_2), .Clk(clk));
  Multiplexer #(.select(2), .width(16), .enable("false")) multiplexer_3 (
    .in0(register_file_1_read_data_1), .in1(Alu_res), .in2(Mem_res), .in3(Write_Back), .out(A),
    .sel(forward_A));
  Multiplexer #(.select(2), .width(16), .enable("false")) multiplexer_4 (
    .in0(register_file_1_read_data_2), .in1(Alu_res), .in2(Mem_res), .in3(Write_Back), .out(B),
    .sel(forward_B));
  ID___EX id_ex_1 (
    .BTA_in(adder_2_out), .OP_in(Op), .Rs(A), .Rt(B), .imm(bit_extender_4_out), .Rd2(multiplexer_1_out),
    .Lui_signal(and_2_out), .BTA_out(id_ex_1_bta_out), .OP_out(id_ex_1_op_out), .Rs_2(id_ex_1_rs_2),
    .Rt_2(id_ex_1_rt_2), .imm_2(id_ex_1_imm_2), .Rd2_2(Rd_ALU), .Lui_signal_2(Lui2),
    .NPC(bit_extender_3_out), .NPC_2(id_ex_1_npc_2), .lui_data(shifter_1_out), .lui_data_2(lui_data_alu),
    .ALU_ctrl_signals(alu_ctrl_unit_1_aluop), .aluOp(aluOp), .inverseA(inverseA), .inverseB(inverseB),
    .control_signals({new_control_unit_1_regwr[6], new_control_unit_1_writedatasrc, new_control_unit_1_regwr[3:0]}),
    .RegWr_ALU(RegWr_ALU), .AluSrc(AluSrc), .Mem_read_alu(Mem_read_alu),
    .control_signals_2(id_ex_1_control_signals_2), .stall(stall), .kill2(Branch), .clk(clk));
  Forward_Unit forward_unit_1 (
    .Rd_ALU(Rd_ALU), .Rd_MEM(Rd_MEM), .Rd_WB(Rd_WB), .Rt(out_2), .Rs(out_1), .Forward_A(forward_A),
    .Forward_B(forward_B), .Mem_Read(Mem_read_alu), .stall(stall), .RW_ALU(RegWr_ALU), .RW_WB(RegWr_WB),
    .RW_MEM(RegWr_MEM));
  Multiplexer #(.width(12), .enable("false")) multiplexer_5 (
    .in0(adder_1_out), .in1(id_ex_1_bta_out), .out(multiplexer_5_out), .sel(Branch));
  Multiplexer #(.width(16), .enable("false")) multiplexer_6 (
    .in0(id_ex_1_rt_2), .in1(id_ex_1_imm_2), .out(multiplexer_6_out), .sel(AluSrc));
  Multiplexer #(.width(12), .enable("false")) multiplexer_7 (
    .in0(multiplexer_5_out), .in1(multiplexer_2_out), .out(multiplexer_7_out), .sel(Jump));
  ALU alu_1 (
    .inverseA(inverseA), .inverseB(inverseB), .A(id_ex_1_rs_2), .B(multiplexer_6_out), .aluOp(aluOp),
    .Result({alu_1_result, lessThan}), .zero(zero), .OverFlow(OverFlow));
  Branch_control branch_control_1 (
    .OverFlow(OverFlow), .op(id_ex_1_op_out), .LT(lessThan), .Zero(zero), .Branch(Branch));
  Multiplexer #(.width(16), .enable("false")) multiplexer_8 (
    .in0({alu_1_result, lessThan}), .in1(lui_data_alu), .out(Alu_res), .sel(Lui2));
  EX___MEM ex_mem_1 (
    .clk(clk), .ALU_Result({alu_1_result, lessThan}), .Data_to_MEM(id_ex_1_rt_2), .Rd3(Rd_ALU),
    .Lui_signal(Lui2), .NPC(id_ex_1_npc_2), .Lui_data(lui_data_alu),
    .control_signals(id_ex_1_control_signals_2), .ALU_Result_2(ex_mem_1_alu_result_2),
    .Data_to_MEM_2(ex_mem_1_data_to_mem_2), .Rd3_2(Rd_MEM), .Lui_signal_2(Lui3), .NPC_2(ex_mem_1_npc_2),
    .Lui_data_2(lui_data_MEM), .control_signals_2(ex_mem_1_control_signals_2), .RegWr_MEM(RegWr_MEM),
    .MemWrite(MemWrite), .MemRead(MemRead), .MemToReg(MemToReg));
  Multiplexer #(.width(16), .enable("false")) multiplexer_9 (
    .in0(multiplexer_10_out), .in1(lui_data_MEM), .out(Mem_res), .sel(Lui3));
  RAM #(.addrWidth(16), .dataWidth(16), .bus("separate")) ram_1 (
    .addr(ex_mem_1_alu_result_2), .din(ex_mem_1_data_to_mem_2), .data(ram_1_data), .str(MemWrite),
    .sel(1'b1), .clk(clk), .ld(MemRead), .clr(1'b0));
  Multiplexer #(.width(16), .enable("false")) multiplexer_10 (
    .in0(ram_1_data), .in1(ex_mem_1_alu_result_2), .out(multiplexer_10_out), .sel(MemToReg));
  MEM___WB mem_wb_1 (
    .Mem_Data_out(multiplexer_10_out), .Rd4(Rd_MEM), .Lui_signal(Lui3), .NPC(ex_mem_1_npc_2),
    .Lui_data(lui_data_MEM), .control_signals(ex_mem_1_control_signals_2),
    .Mem_Data_out_2(mem_wb_1_mem_data_out_2), .Rd4_2(Rd_WB), .WD(WD), .Lui_signal_2(Lui4),
    .Lui_data_2(lui_data_WB), .RegWr_WB(RegWr_WB), .writeDataSrc(writeDataSrc), .in_1(clk));
  Multiplexer #(.width(16), .enable("false")) multiplexer_11 (
    .in0(mem_wb_1_mem_data_out_2), .in1(lui_data_WB), .out(Write_Back), .sel(Lui4));

  // Other names for the same wires on the sheet: Imm6[5:0] = {out_3, Funct};
  //   Imm12[11:0] = {out_1, out_2, out_3, Funct}; Rd[2:0] = out_3; Rt[2:0] = out_2; Rs[2:0] = out_1; kill2 = Branch

  // Notes on the sheet:
  //   contents of rom_1 (hex, n*v repeats v):
  //   a384 8354 35b 2040 2081 20c2 890a 1921 1520 14f2 4c02 1290 403b 3100 b012 55c 1b68 403f 4e9 2040
  //   2285 22c6 4e0 3100 1e06
endmodule

module Register_File (
  input  [2:0] read_register_1,
  input  [2:0] Write_register,
  input  [2:0] read_register_2,
  input  [15:0] Write_Data,
  input  RegWrite,
  input  Clk,
  output [15:0] Read_Data_1,
  output [15:0] Read_Data_2
);

  wire and_1_out, and_2_out, and_3_out, and_4_out, and_5_out, and_6_out, and_7_out, and_8_out,
       decoder_1_out0, decoder_1_out1, decoder_1_out2, decoder_1_out3, decoder_1_out4, decoder_1_out5,
       decoder_1_out6, decoder_1_out7;
  wire [15:0] R0_q, R1_q, R2_q, R3_q, R4_q, R5_q, R6_q, R7_q;

  Decoder #(.select(3), .enable("false")) decoder_1 (
    .out0(decoder_1_out0), .out1(decoder_1_out1), .out2(decoder_1_out2), .out3(decoder_1_out3),
    .out4(decoder_1_out4), .out5(decoder_1_out5), .out6(decoder_1_out6), .out7(decoder_1_out7),
    .sel(Write_register));
  and and_1 (and_1_out, decoder_1_out0, RegWrite);
  and and_2 (and_2_out, decoder_1_out1, RegWrite);
  and and_3 (and_3_out, decoder_1_out2, RegWrite);
  and and_4 (and_4_out, decoder_1_out3, RegWrite);
  and and_5 (and_5_out, decoder_1_out4, RegWrite);
  and and_6 (and_6_out, decoder_1_out5, RegWrite);
  and and_7 (and_7_out, decoder_1_out6, RegWrite);
  and and_8 (and_8_out, decoder_1_out7, RegWrite);
  Register #(.width(16)) R0 (.D({16{1'b0}}), .en(and_1_out), .Q(R0_q), .clk(Clk));  // open: clr
  Register #(.width(16)) R1 (.D(Write_Data), .en(and_2_out), .Q(R1_q), .clk(Clk));  // open: clr
  Register #(.width(16)) R2 (.D(Write_Data), .en(and_3_out), .Q(R2_q), .clk(Clk));  // open: clr
  Register #(.width(16)) R3 (.D(Write_Data), .en(and_4_out), .Q(R3_q), .clk(Clk));  // open: clr
  Register #(.width(16)) R4 (.D(Write_Data), .en(and_5_out), .Q(R4_q), .clk(Clk));  // open: clr
  Register #(.width(16)) R5 (.D(Write_Data), .en(and_6_out), .Q(R5_q), .clk(Clk));  // open: clr
  Register #(.width(16)) R6 (.D(Write_Data), .en(and_7_out), .Q(R6_q), .clk(Clk));  // open: clr
  Register #(.width(16)) R7 (.D(Write_Data), .en(and_8_out), .Q(R7_q), .clk(Clk));  // open: clr
  Multiplexer #(.select(3), .width(16), .enable("false")) multiplexer_1 (
    .in0(R0_q), .in1(R1_q), .in2(R2_q), .in3(R3_q), .in4(R4_q), .in5(R5_q), .in6(R6_q), .in7(R7_q),
    .out(Read_Data_1), .sel(read_register_1));
  Multiplexer #(.select(3), .width(16), .enable("false")) multiplexer_2 (
    .in0(R0_q), .in1(R1_q), .in2(R2_q), .in3(R3_q), .in4(R4_q), .in5(R5_q), .in6(R6_q), .in7(R7_q),
    .out(Read_Data_2), .sel(read_register_2));
endmodule

module ALU (
  input  inverseA,
  input  inverseB,
  input  [15:0] A,
  input  [15:0] B,
  input  [3:0] aluOp,
  output [15:0] Result,
  output zero,
  output OverFlow
);

  wire [0:0] and_2_out, or_2_out, or_3_out;
  wire [15:0] adder_1_out, and_1_out, multiplexer_1_out, multiplexer_2_out, not_1_out, not_2_out, or_1_out,
       shifter_1_out, shifter_2_out, shifter_3_out, shifter_4_out, xor_1_out;

  assign not_1_out = ~A;  // NOT_Gate not_1, 16 bits wide
  assign not_2_out = ~B;  // NOT_Gate not_2, 16 bits wide
  Multiplexer #(.width(16), .enable("false")) multiplexer_1 (
    .in0(A), .in1(not_1_out), .out(multiplexer_1_out), .sel(inverseA));
  Multiplexer #(.width(16), .enable("false")) multiplexer_2 (
    .in0(B), .in1(not_2_out), .out(multiplexer_2_out), .sel(inverseB));
  adder adder_1 (.A(multiplexer_1_out), .B(multiplexer_2_out), .overFlow(OverFlow), .out(adder_1_out), .C_in(inverseB));
  assign and_1_out = multiplexer_1_out & multiplexer_2_out;  // AND_Gate and_1, 16 bits wide
  assign or_1_out = multiplexer_1_out | multiplexer_2_out;  // OR_Gate or_1, 16 bits wide
  assign xor_1_out = multiplexer_1_out ^ multiplexer_2_out;  // XOR_Gate xor_1, 16 bits wide
  Shifter #(.width(16)) shifter_1 (.in(multiplexer_1_out), .\dist (multiplexer_2_out[3:0]), .out(shifter_1_out));
  Shifter #(.width(16), .shift("lr")) shifter_2 (
    .in(multiplexer_1_out), .\dist (multiplexer_2_out[3:0]), .out(shifter_2_out));
  Shifter #(.width(16), .shift("ar")) shifter_3 (
    .in(multiplexer_1_out), .\dist (multiplexer_2_out[3:0]), .out(shifter_3_out));
  Shifter #(.width(16), .shift("rl")) shifter_4 (
    .in(multiplexer_1_out), .\dist (multiplexer_2_out[3:0]), .out(shifter_4_out));
  and and_2 (and_2_out[0], OverFlow, adder_1_out[15]);
  or or_2 (or_2_out[0], zero, and_2_out[0]);
  or or_3 (or_3_out[0], zero, adder_1_out[15]);
  Multiplexer #(.select(4), .width(16), .enable("false")) multiplexer_3 (
    .in0(adder_1_out), .in1(and_1_out), .in2(or_1_out), .in3(xor_1_out), .in4(shifter_1_out),
    .in5(shifter_2_out), .in6(shifter_3_out), .in7(shifter_4_out), .in8({{15{1'b0}}, adder_1_out[15]}),
    .in9({{15{1'b0}}, and_2_out[0]}), .in10({{15{1'b0}}, or_3_out[0]}), .in11({{15{1'b0}}, or_2_out[0]}),
    .out(Result), .sel(aluOp));  // open: in12, in13, in14, in15
  nor nor_1 (zero, adder_1_out[0], adder_1_out[1], adder_1_out[2], adder_1_out[3], adder_1_out[4], adder_1_out[5], adder_1_out[6], adder_1_out[7], adder_1_out[9], adder_1_out[10], adder_1_out[11], adder_1_out[12], adder_1_out[13], adder_1_out[14], adder_1_out[15], adder_1_out[8]);
endmodule

module adder (
  input  C_in,
  input  [15:0] A,
  input  [15:0] B,
  output [15:0] out,
  output overFlow
);

  wire adder_1_cout, adder_2_cout, adder_3_cout, adder_4_cout, adder_5_cout, adder_6_cout, adder_7_cout,
       adder_8_cout, adder_9_cout, adder_10_cout, adder_11_cout, adder_12_cout, adder_13_cout, adder_14_cout,
       adder_15_cout, adder_16_cout;

  Adder #(.width(1)) adder_1 (.a(A[0]), .b(B[0]), .out(out[0]), .cin(C_in), .cout(adder_1_cout));
  Adder #(.width(1)) adder_2 (.a(A[1]), .b(B[1]), .out(out[1]), .cin(adder_1_cout), .cout(adder_2_cout));
  Adder #(.width(1)) adder_3 (.a(A[2]), .b(B[2]), .out(out[2]), .cin(adder_2_cout), .cout(adder_3_cout));
  Adder #(.width(1)) adder_4 (.a(A[3]), .b(B[3]), .out(out[3]), .cin(adder_3_cout), .cout(adder_4_cout));
  Adder #(.width(1)) adder_5 (.a(A[4]), .b(B[4]), .out(out[4]), .cin(adder_4_cout), .cout(adder_5_cout));
  Adder #(.width(1)) adder_6 (.a(A[5]), .b(B[5]), .out(out[5]), .cin(adder_5_cout), .cout(adder_6_cout));
  Adder #(.width(1)) adder_7 (.a(A[6]), .b(B[6]), .out(out[6]), .cin(adder_6_cout), .cout(adder_7_cout));
  Adder #(.width(1)) adder_8 (.a(A[7]), .b(B[7]), .out(out[7]), .cin(adder_7_cout), .cout(adder_8_cout));
  Adder #(.width(1)) adder_9 (.a(A[8]), .b(B[8]), .out(out[8]), .cin(adder_8_cout), .cout(adder_9_cout));
  Adder #(.width(1)) adder_10 (.a(A[9]), .b(B[9]), .out(out[9]), .cin(adder_9_cout), .cout(adder_10_cout));
  Adder #(.width(1)) adder_11 (.a(A[10]), .b(B[10]), .out(out[10]), .cin(adder_10_cout), .cout(adder_11_cout));
  Adder #(.width(1)) adder_12 (.a(A[11]), .b(B[11]), .out(out[11]), .cin(adder_11_cout), .cout(adder_12_cout));
  Adder #(.width(1)) adder_13 (.a(A[12]), .b(B[12]), .out(out[12]), .cin(adder_12_cout), .cout(adder_13_cout));
  Adder #(.width(1)) adder_14 (.a(A[13]), .b(B[13]), .out(out[13]), .cin(adder_13_cout), .cout(adder_14_cout));
  Adder #(.width(1)) adder_15 (.a(A[14]), .b(B[14]), .out(out[14]), .cin(adder_14_cout), .cout(adder_15_cout));
  Adder #(.width(1)) adder_16 (.a(A[15]), .b(B[15]), .out(out[15]), .cin(adder_15_cout), .cout(adder_16_cout));
  xor xor_1 (overFlow, adder_15_cout, adder_16_cout);
endmodule

module Control_Unit1 (
  input  [3:0] op,
  input  [2:0] Func,
  output RegWr,
  output AluSrc,
  output MemWrite,
  output MemRead,
  output Jump,
  output JumpSrc,
  output [1:0] RegDst,
  output [1:0] writeDataSrc,
  output MemToReg
);

  wire and_2_out, and_3_out, and_4_out, and_5_out, and_6_out, and_7_out, and_8_out, and_9_out, and_12_out,
       and_13_out, and_14_out, and_15_out, and_16_out, and_17_out, and_18_out, and_19_out, and_20_out,
       and_21_out, and_22_out, and_23_out, and_24_out, and_25_out, not_1_out, not_2_out, not_3_out,
       not_4_out, not_5_out, not_6_out, not_7_out, not_8_out, not_9_out, not_10_out, not_11_out, not_12_out,
       not_13_out, not_14_out, not_15_out, not_16_out, not_17_out, not_18_out, not_19_out, not_20_out,
       not_21_out, not_22_out, not_23_out, not_24_out, not_25_out, not_26_out, not_27_out, not_28_out,
       not_30_out, not_31_out, not_32_out, not_33_out, not_34_out, not_35_out, not_36_out, not_37_out,
       not_38_out, not_39_out, not_40_out, not_41_out;

  not not_1 (not_1_out, op[3]);
  not not_2 (not_2_out, op[2]);
  not not_3 (not_3_out, op[1]);
  not not_4 (not_4_out, Func[2]);
  not not_5 (not_5_out, op[3]);
  not not_6 (not_6_out, op[2]);
  not not_7 (not_7_out, op[1]);
  not not_8 (not_8_out, Func[1]);
  not not_9 (not_9_out, op[2]);
  not not_10 (not_10_out, op[0]);
  not not_11 (not_11_out, op[3]);
  not not_12 (not_12_out, op[2]);
  not not_13 (not_13_out, op[1]);
  not not_14 (not_14_out, op[3]);
  not not_15 (not_15_out, op[2]);
  not not_16 (not_16_out, op[3]);
  not not_17 (not_17_out, op[2]);
  not not_18 (not_18_out, op[3]);
  not not_19 (not_19_out, op[2]);
  not not_20 (not_20_out, op[0]);
  not not_21 (not_21_out, op[2]);
  not not_22 (not_22_out, op[1]);
  not not_23 (not_23_out, op[2]);
  not not_24 (not_24_out, op[1]);
  not not_25 (not_25_out, op[2]);
  not not_26 (not_26_out, Func[2]);
  not not_27 (not_27_out, Func[1]);
  not not_28 (not_28_out, Func[0]);
  not not_29 (JumpSrc, op[3]);
  and and_1 (RegDst[1], op[3], op[1]);
  not not_30 (not_30_out, op[3]);
  not not_31 (not_31_out, op[1]);
  not not_32 (not_32_out, op[2]);
  not not_33 (not_33_out, op[2]);
  not not_34 (not_34_out, op[2]);
  not not_35 (not_35_out, op[0]);
  not not_36 (not_36_out, op[0]);
  not not_37 (not_37_out, op[1]);
  not not_38 (not_38_out, Func[2]);
  not not_39 (not_39_out, Func[1]);
  not not_40 (not_40_out, Func[0]);
  not not_41 (not_41_out, op[1]);
  and and_2 (and_2_out, not_1_out, not_2_out, not_3_out, not_4_out);
  and and_3 (and_3_out, not_5_out, not_6_out, not_7_out, not_8_out);
  and and_4 (and_4_out, not_9_out, not_10_out);
  and and_5 (and_5_out, not_11_out, not_12_out, not_13_out, Func[0]);
  and and_6 (and_6_out, not_14_out, op[2], op[1]);
  and and_7 (and_7_out, op[3], not_15_out, op[1]);
  and and_8 (and_8_out, not_16_out, op[1]);
  and and_9 (and_9_out, op[3], not_17_out);
  and and_10 (MemWrite, not_18_out, not_19_out, op[1], op[0]);
  and and_11 (MemRead, op[1], not_20_out);
  and and_12 (and_12_out, not_21_out, not_22_out, op[0], Func[2], Func[1]);
  and and_13 (and_13_out, op[3], not_23_out, not_24_out, op[0]);
  and and_14 (and_14_out, op[3], not_25_out, op[0], not_26_out, not_27_out, not_28_out);
  and and_15 (and_15_out, not_30_out, not_31_out);
  and and_16 (and_16_out, not_32_out, op[0], Func[0]);
  and and_17 (and_17_out, not_33_out, op[0], Func[1]);
  and and_18 (and_18_out, not_34_out, op[0], Func[2]);
  and and_19 (and_19_out, op[3], op[1], not_35_out);
  and and_20 (and_20_out, op[3], op[1], not_36_out);
  and and_21 (and_21_out, op[3], op[1], Func[0]);
  and and_22 (and_22_out, op[3], op[1], Func[1]);
  and and_23 (and_23_out, op[3], op[1], Func[2]);
  and and_24 (and_24_out, not_37_out, op[0], Func[2], Func[1], Func[0]);
  and and_25 (and_25_out, op[3], op[0], not_38_out, not_39_out, not_40_out);
  or or_1 (MemToReg, not_41_out, op[2]);
  or or_2 (RegWr, and_2_out, and_3_out, and_4_out, and_5_out, and_6_out, and_7_out);
  or or_3 (AluSrc, and_8_out, and_9_out);
  or or_4 (Jump, and_12_out, and_13_out, and_14_out);
  or or_5 (RegDst[0], and_15_out, and_16_out, and_17_out, and_18_out, and_19_out);
  or or_6 (writeDataSrc[1], and_20_out, and_21_out, and_22_out, and_23_out);
  or or_7 (writeDataSrc[0], and_24_out, and_25_out);
endmodule

module ALU_CTRL_Unit (
  input  [3:0] Op,
  input  [2:0] func,
  output [3:0] aluop,
  output inversA,
  output inversB
);

  wire and_1_out, and_2_out, and_4_out, and_5_out, and_6_out, and_7_out, and_8_out, and_9_out, and_10_out,
       and_11_out, and_13_out, and_14_out, and_15_out, and_16_out, and_17_out, not_1_out, not_2_out,
       not_3_out, not_4_out, not_5_out, not_6_out, not_7_out, not_8_out, not_9_out, not_10_out, not_11_out,
       not_12_out, not_13_out, not_14_out, not_15_out, not_16_out, not_17_out, not_18_out, not_19_out,
       not_20_out, not_21_out, not_22_out, not_23_out, not_24_out, not_25_out, not_26_out, not_27_out,
       not_28_out, not_29_out, not_30_out, not_31_out, not_32_out, not_33_out, not_34_out, not_35_out,
       not_36_out, not_37_out, not_38_out, not_39_out, not_40_out, not_41_out, not_42_out, not_43_out,
       not_44_out, not_45_out, not_46_out;

  not not_1 (not_1_out, Op[2]);
  not not_2 (not_2_out, Op[1]);
  not not_3 (not_3_out, Op[2]);
  not not_4 (not_4_out, Op[1]);
  not not_5 (not_5_out, Op[3]);
  not not_6 (not_6_out, Op[2]);
  not not_7 (not_7_out, Op[1]);
  not not_8 (not_8_out, Op[0]);
  not not_9 (not_9_out, Op[3]);
  not not_10 (not_10_out, Op[2]);
  not not_11 (not_11_out, Op[1]);
  not not_12 (not_12_out, Op[0]);
  not not_13 (not_13_out, func[2]);
  not not_14 (not_14_out, Op[3]);
  not not_15 (not_15_out, Op[2]);
  not not_16 (not_16_out, Op[1]);
  not not_17 (not_17_out, Op[2]);
  not not_18 (not_18_out, Op[1]);
  not not_19 (not_19_out, Op[3]);
  not not_20 (not_20_out, Op[3]);
  not not_21 (not_21_out, Op[2]);
  not not_22 (not_22_out, Op[1]);
  not not_23 (not_23_out, Op[0]);
  not not_24 (not_24_out, func[2]);
  not not_25 (not_25_out, func[0]);
  not not_26 (not_26_out, Op[3]);
  not not_27 (not_27_out, Op[2]);
  not not_28 (not_28_out, Op[1]);
  not not_29 (not_29_out, Op[3]);
  not not_30 (not_30_out, Op[2]);
  not not_31 (not_31_out, Op[1]);
  not not_32 (not_32_out, Op[3]);
  not not_33 (not_33_out, Op[0]);
  not not_34 (not_34_out, Op[3]);
  not not_35 (not_35_out, Op[2]);
  not not_36 (not_36_out, Op[1]);
  not not_37 (not_37_out, Op[0]);
  not not_38 (not_38_out, func[2]);
  not not_39 (not_39_out, func[0]);
  not not_40 (not_40_out, Op[3]);
  not not_41 (not_41_out, Op[1]);
  not not_42 (not_42_out, func[2]);
  not not_43 (not_43_out, func[0]);
  not not_44 (not_44_out, Op[1]);
  not not_45 (not_45_out, Op[1]);
  not not_46 (not_46_out, Op[1]);
  and and_1 (and_1_out, not_1_out, not_2_out, Op[0], func[1]);
  and and_2 (and_2_out, not_3_out, not_4_out, Op[0], func[2]);
  and and_3 (aluop[2], not_5_out, not_6_out, not_7_out, not_8_out, func[2]);
  and and_4 (and_4_out, not_9_out, not_10_out, not_11_out, not_12_out, not_13_out, func[0]);
  and and_5 (and_5_out, not_14_out, not_15_out, not_16_out, func[2], func[1]);
  and and_6 (and_6_out, not_17_out, not_18_out, Op[0], func[2]);
  and and_7 (and_7_out, not_19_out, Op[2], Op[1], Op[0]);
  and and_8 (and_8_out, not_20_out, not_21_out, not_22_out, not_23_out, not_24_out, not_25_out);
  and and_9 (and_9_out, not_26_out, not_27_out, not_28_out, func[1], func[0]);
  and and_10 (and_10_out, not_29_out, not_30_out, not_31_out, func[2], func[0]);
  and and_11 (and_11_out, not_32_out, Op[2], Op[1], not_33_out);
  and and_12 (inversA, not_34_out, not_35_out, not_36_out, not_37_out, not_38_out, func[1], not_39_out);
  and and_13 (and_13_out, not_40_out, not_41_out, not_42_out, func[1], not_43_out);
  and and_14 (and_14_out, not_44_out, Op[0], func[0]);
  and and_15 (and_15_out, not_45_out, Op[0], func[2]);
  and and_16 (and_16_out, Op[2], not_46_out);
  and and_17 (and_17_out, Op[3], Op[1]);
  or or_1 (aluop[3], and_1_out, and_2_out);
  or or_2 (aluop[1], and_4_out, and_5_out, and_6_out, and_7_out);
  or or_3 (aluop[0], and_8_out, and_9_out, and_10_out, and_11_out);
  or or_4 (inversB, and_13_out, and_14_out, and_15_out, and_16_out, and_17_out);
endmodule

module Branch_control (
  input  OverFlow,
  input  [3:0] op,
  input  LT,
  input  Zero,
  output Branch
);

  wire and_1_out, and_2_out, and_3_out, and_4_out, not_1_out, not_2_out, not_3_out, not_4_out, not_5_out,
       not_6_out, not_7_out, not_8_out, not_9_out, not_10_out, not_11_out, not_12_out, not_13_out;

  not not_1 (not_1_out, OverFlow);
  not not_2 (not_2_out, op[3]);
  not not_3 (not_3_out, op[1]);
  not not_4 (not_4_out, op[0]);
  not not_5 (not_5_out, OverFlow);
  not not_6 (not_6_out, op[3]);
  not not_7 (not_7_out, op[1]);
  not not_8 (not_8_out, Zero);
  not not_9 (not_9_out, OverFlow);
  not not_10 (not_10_out, op[1]);
  not not_11 (not_11_out, op[0]);
  not not_12 (not_12_out, OverFlow);
  not not_13 (not_13_out, LT);
  and and_1 (and_1_out, not_1_out, not_2_out, op[2], not_3_out, not_4_out, Zero);
  and and_2 (and_2_out, not_5_out, not_6_out, op[2], not_7_out, op[0], not_8_out);
  and and_3 (and_3_out, not_9_out, op[3], op[2], not_10_out, not_11_out, LT);
  and and_4 (and_4_out, not_12_out, op[3], op[2], op[1], not_13_out);
  or or_1 (Branch, and_1_out, and_2_out, and_3_out, and_4_out);
endmodule

module new_branch_control (
  input  [15:0] Rs,
  input  [4:0] OP,
  input  [15:0] Rt,
  output branch
);

  wire and_1_out, and_2_out, and_3_out, and_4_out, and_5_out, and_6_out, and_7_out, comparator_1_eq,
       comparator_1_gt, comparator_1_lt, not_1_out, not_2_out, not_3_out, not_4_out, not_5_out, not_6_out,
       not_7_out, not_8_out, not_9_out, or_4_out, or_5_out;
  wire [2:0] or_3_out;

  not not_1 (not_1_out, OP[0]);
  not not_2 (not_2_out, OP[1]);
  not not_3 (not_3_out, OP[1]);
  not not_4 (not_4_out, OP[3]);
  not not_5 (not_5_out, OP[1]);
  not not_6 (not_6_out, OP[0]);
  not not_7 (not_7_out, OP[1]);
  not not_8 (not_8_out, OP[0]);
  and and_1 (and_1_out, OP[4], OP[3], OP[2], not_1_out);
  and and_2 (and_2_out, OP[4], OP[3], OP[2], OP[1]);
  and and_3 (and_3_out, OP[4], OP[2], not_2_out, OP[0]);
  and and_4 (and_4_out, OP[4], OP[3], OP[2], not_3_out);
  and and_5 (and_5_out, OP[4], not_4_out, OP[2], not_5_out, not_6_out);
  and and_6 (and_6_out, OP[4], OP[3], OP[2], not_7_out, OP[0]);
  and and_7 (and_7_out, OP[4], OP[3], OP[2], OP[1], not_8_out);
  or or_1 (or_3_out[2], and_1_out, and_2_out);
  or or_2 (or_3_out[1], and_3_out, and_4_out);
  or or_3 (or_3_out[0], and_5_out, and_6_out, and_7_out);
  Comparator #(.width(16)) comparator_1 (
    .a(Rs), .b(Rt), .gt(comparator_1_gt), .eq(comparator_1_eq), .lt(comparator_1_lt));
  not not_9 (not_9_out, comparator_1_eq);
  or or_4 (or_4_out, comparator_1_gt, comparator_1_eq);
  or or_5 (or_5_out, comparator_1_eq, comparator_1_lt);
  Multiplexer #(.select(3), .enable("false")) multiplexer_1 (
    .in0(1'b0), .in1(comparator_1_eq), .in2(not_9_out), .in3(comparator_1_lt), .in4(comparator_1_gt),
    .in5(or_4_out), .in6(or_5_out), .in7(1'b0), .out(branch), .sel(or_3_out));
endmodule

module Forward_Unit (
  input  RW_ALU,
  input  RW_MEM,
  input  RW_WB,
  input  [2:0] Rd_ALU,
  input  [2:0] Rd_MEM,
  input  [2:0] Rd_WB,
  input  [2:0] Rt,
  input  [2:0] Rs,
  input  Mem_Read,
  output [1:0] Forward_A,
  output [1:0] Forward_B,
  output stall
);

  wire comparator_1_eq, comparator_2_eq, comparator_3_eq, or_1_out, Rd_ALU_t, Rd_MEM_t, Rd_WB_t, Rs_Alu,
       Rs_MEM, Rs_WB, Rt_Alu, Rt_MEM, Rt_WB;
  wire [2:0] and_2_out, and_5_out;

  Comparator #(.width(3)) comparator_1 (.a(Rd_WB), .b(3'b000), .eq(comparator_1_eq));  // open: gt, lt
  Comparator #(.width(3)) comparator_2 (.a(Rd_ALU), .b(3'b000), .eq(comparator_2_eq));  // open: gt, lt
  Comparator #(.width(3)) comparator_3 (.a(Rd_MEM), .b(3'b000), .eq(comparator_3_eq));  // open: gt, lt
  or or_1 (or_1_out, Rt_Alu, Rs_Alu);
  not not_1 (Rd_ALU_t, comparator_2_eq);
  not not_2 (Rd_MEM_t, comparator_3_eq);
  not not_3 (Rd_WB_t, comparator_1_eq);
  Comparator #(.width(3)) comparator_4 (.a(Rs), .b(Rd_ALU), .eq(Rs_Alu));  // open: gt, lt
  Comparator #(.width(3)) comparator_5 (.a(Rs), .b(Rd_MEM), .eq(Rs_MEM));  // open: gt, lt
  Comparator #(.width(3)) comparator_6 (.a(Rs), .b(Rd_WB), .eq(Rs_WB));  // open: gt, lt
  Comparator #(.width(3)) comparator_7 (.a(Rt), .b(Rd_ALU), .eq(Rt_Alu));  // open: gt, lt
  Comparator #(.width(3)) comparator_8 (.a(Rt), .b(Rd_MEM), .eq(Rt_MEM));  // open: gt, lt
  Comparator #(.width(3)) comparator_9 (.a(Rt), .b(Rd_WB), .eq(Rt_WB));  // open: gt, lt
  and and_1 (stall, Mem_Read, or_1_out);
  and and_2 (and_2_out[0], Rs_Alu, RW_ALU, Rd_ALU_t);
  and and_3 (and_2_out[1], Rs_MEM, RW_MEM, Rd_MEM_t);
  and and_4 (and_2_out[2], Rs_WB, RW_WB, Rd_WB_t);
  and and_5 (and_5_out[0], Rt_Alu, RW_ALU, Rd_ALU_t);
  and and_6 (and_5_out[1], Rt_MEM, RW_MEM, Rd_MEM_t);
  and and_7 (and_5_out[2], Rt_WB, RW_WB, Rd_WB_t);
  Multiplexer #(.select(3), .width(2), .enable("false")) multiplexer_1 (
    .in0(2'b00), .in1(2'b01), .in2(2'b10), .in3(2'b01), .in4(2'b11), .in5(2'b01), .in6(2'b10), .in7(2'b01),
    .out(Forward_A), .sel(and_2_out));
  Multiplexer #(.select(3), .width(2), .enable("false")) multiplexer_2 (
    .in0(2'b00), .in1(2'b01), .in2(2'b10), .in3(2'b01), .in4(2'b11), .in5(2'b01), .in6(2'b10), .in7(2'b01),
    .out(Forward_B), .sel(and_5_out));
endmodule

module IF_ID (
  input  [11:0] NPC,
  input  [15:0] instruction_in,
  input  kill1,
  input  stall,
  input  clk,
  output [11:0] NPC_2,
  output [15:0] instruction_out
);

  wire not_1_out;
  wire [15:0] multiplexer_1_out;

  Multiplexer #(.width(16), .enable("false")) multiplexer_1 (
    .in0(instruction_in), .in1({16{1'b0}}), .out(multiplexer_1_out), .sel(kill1));
  not not_1 (not_1_out, stall);
  Register #(.width(12)) u_NPC (.D(NPC), .en(1'b1), .Q(NPC_2), .clk(clk));  // open: clr
  Register #(.width(16)) Instruc (.D(multiplexer_1_out), .en(not_1_out), .Q(instruction_out), .clk(clk));  // open: clr
endmodule

module ID___EX (
  input  clk,
  input  [11:0] BTA_in,
  input  [3:0] OP_in,
  input  [15:0] Rs,
  input  [15:0] Rt,
  input  [15:0] imm,
  input  [2:0] Rd2,
  input  Lui_signal,
  input  [15:0] NPC,
  input  [15:0] lui_data,
  input  [5:0] ALU_ctrl_signals,
  input  [6:0] control_signals,
  input  stall,
  input  kill2,
  output [11:0] BTA_out,
  output [3:0] OP_out,
  output [15:0] Rs_2,
  output [15:0] Rt_2,
  output [15:0] imm_2,
  output [2:0] Rd2_2,
  output Lui_signal_2,
  output [15:0] NPC_2,
  output [15:0] lui_data_2,
  output [3:0] aluOp,
  output inverseA,
  output inverseB,
  output [6:0] control_signals_2,
  output RegWr_ALU,
  output AluSrc,
  output Mem_read_alu
);

  wire or_1_out;
  wire [6:0] multiplexer_1_out;

  or or_1 (or_1_out, stall, kill2);
  Multiplexer #(.width(7), .enable("false")) multiplexer_1 (
    .in0(control_signals), .in1({7{1'b0}}), .out(multiplexer_1_out), .sel(or_1_out));
  Register #(.width(12)) Branch_Target_Address (.D(BTA_in), .en(1'b1), .Q(BTA_out), .clk(clk));  // open: clr
  Register #(.width(4)) register_1 (.D(OP_in), .en(1'b1), .Q(OP_out), .clk(clk));  // open: clr
  Register #(.width(16)) A (.D(Rs), .en(1'b1), .Q(Rs_2), .clk(clk));  // open: clr
  Register #(.width(16)) B (.D(Rt), .en(1'b1), .Q(Rt_2), .clk(clk));  // open: clr
  Register #(.width(16)) u_imm (.D(imm), .en(1'b1), .Q(imm_2), .clk(clk));  // open: clr
  Register #(.width(3)) u_Rd2 (.D(Rd2), .en(1'b1), .Q(Rd2_2), .clk(clk));  // open: clr
  Register #(.width(1)) u_Lui_signal (.D(Lui_signal), .en(1'b1), .Q(Lui_signal_2), .clk(clk));  // open: clr
  Register #(.width(16)) register_2 (.D(NPC), .en(1'b1), .Q(NPC_2), .clk(clk));  // open: clr
  Register #(.width(16)) u_lui_data (.D(lui_data), .en(1'b1), .Q(lui_data_2), .clk(clk));  // open: clr
  Register #(.width(6)) u_ALU_ctrl_signals (
    .D(ALU_ctrl_signals), .en(1'b1), .Q({inverseB, inverseA, aluOp}), .clk(clk));  // open: clr
  Register #(.width(7)) u_control_signals (
    .D(multiplexer_1_out), .en(1'b1), .Q({control_signals_2[6:2], AluSrc, control_signals_2[0]}), .clk(clk));  // open: clr

  assign control_signals_2[1] = AluSrc;
  assign Mem_read_alu = control_signals_2[3];
  assign RegWr_ALU = control_signals_2[0];
endmodule

module EX___MEM (
  input  clk,
  input  [15:0] ALU_Result,
  input  [15:0] Data_to_MEM,
  input  [2:0] Rd3,
  input  Lui_signal,
  input  [15:0] NPC,
  input  [15:0] Lui_data,
  input  [6:0] control_signals,
  output [15:0] ALU_Result_2,
  output [15:0] Data_to_MEM_2,
  output [2:0] Rd3_2,
  output Lui_signal_2,
  output [15:0] NPC_2,
  output [15:0] Lui_data_2,
  output [6:0] control_signals_2,
  output RegWr_MEM,
  output MemWrite,
  output MemRead,
  output MemToReg
);

  Register #(.width(16)) u_ALU_Result (.D(ALU_Result), .en(1'b1), .Q(ALU_Result_2), .clk(clk));  // open: clr
  Register #(.width(16)) u_Data_to_MEM (.D(Data_to_MEM), .en(1'b1), .Q(Data_to_MEM_2), .clk(clk));  // open: clr
  Register #(.width(3)) u_Rd3 (.D(Rd3), .en(1'b1), .Q(Rd3_2), .clk(clk));  // open: clr
  Register #(.width(1)) u_Lui_signal (.D(Lui_signal), .en(1'b1), .Q(Lui_signal_2), .clk(clk));  // open: clr
  Register #(.width(16)) u_NPC (.D(NPC), .en(1'b1), .Q(NPC_2), .clk(clk));  // open: clr
  Register #(.width(16)) u_Lui_data (.D(Lui_data), .en(1'b1), .Q(Lui_data_2), .clk(clk));  // open: clr
  Register #(.width(7)) u_control_signals (
    .D(control_signals), .en(1'b1), .Q(control_signals_2), .clk(clk));  // open: clr

  assign MemRead = control_signals_2[3];
  assign MemToReg = control_signals_2[6];
  assign MemWrite = control_signals_2[2];
  assign RegWr_MEM = control_signals_2[0];
endmodule

module MEM___WB (
  input  in_1,
  input  [15:0] Mem_Data_out,
  input  [2:0] Rd4,
  input  Lui_signal,
  input  [15:0] NPC,
  input  [15:0] Lui_data,
  input  [6:0] control_signals,
  output [15:0] Mem_Data_out_2,
  output [2:0] Rd4_2,
  output [15:0] WD,
  output Lui_signal_2,
  output [15:0] Lui_data_2,
  output RegWr_WB,
  output [1:0] writeDataSrc
);

  wire [6:1] control_signals_q;
  wire [15:0] NPC_q;

  Register #(.width(16)) u_Mem_Data_out (.D(Mem_Data_out), .en(1'b1), .Q(Mem_Data_out_2), .clk(in_1));  // open: clr
  Register #(.width(3)) u_Rd4 (.D(Rd4), .en(1'b1), .Q(Rd4_2), .clk(in_1));  // open: clr
  Register #(.width(1)) u_Lui_signal (.D(Lui_signal), .en(1'b1), .Q(Lui_signal_2), .clk(in_1));  // open: clr
  Register #(.width(16)) u_NPC (.D(NPC), .en(1'b1), .Q(NPC_q), .clk(in_1));  // open: clr
  Register #(.width(16)) u_Lui_data (.D(Lui_data), .en(1'b1), .Q(Lui_data_2), .clk(in_1));  // open: clr
  Register #(.width(7)) u_control_signals (
    .D(control_signals), .en(1'b1),
    .Q({control_signals_q[6], writeDataSrc, control_signals_q[3:1], RegWr_WB}), .clk(in_1));  // open: clr
  Multiplexer #(.select(2), .width(16), .enable("false")) multiplexer_1 (
    .in0(Mem_Data_out_2), .in1(NPC_q), .in2(Lui_data_2), .out(WD), .sel(writeDataSrc));  // open: in3

  // Other names for the same wires on the sheet: clk = in_1
endmodule

module new_control_unit (
  input  [3:0] op,
  input  [2:0] Func,
  output RegWr,
  output Alurc,
  output MemWrite,
  output MemRead,
  output Jump,
  output Jump_Src,
  output [1:0] RegDst,
  output [1:0] writeDataSrc,
  output MemToReg
);

  wire and_2_out, and_3_out, and_4_out, and_5_out, and_6_out, and_7_out, and_8_out, and_9_out, and_12_out,
       and_13_out, and_14_out, and_15_out, and_17_out, and_18_out, not_1_out, not_2_out, not_3_out,
       not_4_out, not_5_out, not_6_out, not_7_out, not_8_out, not_9_out, not_10_out, not_11_out, not_12_out,
       not_13_out, not_14_out, not_15_out, not_16_out, not_17_out, not_18_out, not_19_out, not_20_out,
       not_21_out, not_22_out, not_23_out, not_25_out, not_26_out, not_27_out, not_28_out, not_29_out,
       not_30_out;

  not not_1 (not_1_out, op[3]);
  not not_2 (not_2_out, op[2]);
  not not_3 (not_3_out, op[1]);
  not not_4 (not_4_out, Func[2]);
  not not_5 (not_5_out, op[3]);
  not not_6 (not_6_out, op[2]);
  not not_7 (not_7_out, op[1]);
  not not_8 (not_8_out, Func[1]);
  not not_9 (not_9_out, op[2]);
  not not_10 (not_10_out, op[0]);
  not not_11 (not_11_out, op[3]);
  not not_12 (not_12_out, op[2]);
  not not_13 (not_13_out, op[1]);
  not not_14 (not_14_out, op[3]);
  not not_15 (not_15_out, op[2]);
  not not_16 (not_16_out, op[3]);
  not not_17 (not_17_out, op[2]);
  not not_18 (not_18_out, op[3]);
  not not_19 (not_19_out, op[2]);
  not not_20 (not_20_out, op[0]);
  not not_21 (not_21_out, op[2]);
  not not_22 (not_22_out, op[1]);
  not not_23 (not_23_out, op[2]);
  not not_24 (Jump_Src, op[3]);
  and and_1 (RegDst[1], op[3], op[1]);
  not not_25 (not_25_out, op[3]);
  not not_26 (not_26_out, op[1]);
  not not_27 (not_27_out, op[0]);
  not not_28 (not_28_out, op[0]);
  not not_29 (not_29_out, op[2]);
  not not_30 (not_30_out, op[1]);
  and and_2 (and_2_out, not_1_out, not_2_out, not_3_out, not_4_out);
  and and_3 (and_3_out, not_5_out, not_6_out, not_7_out, not_8_out);
  and and_4 (and_4_out, not_9_out, not_10_out);
  and and_5 (and_5_out, not_11_out, not_12_out, not_13_out, Func[0]);
  and and_6 (and_6_out, not_14_out, op[2], op[1]);
  and and_7 (and_7_out, op[3], not_15_out, op[1]);
  and and_8 (and_8_out, not_16_out, op[1]);
  and and_9 (and_9_out, op[3], not_17_out);
  and and_10 (MemWrite, not_18_out, not_19_out, op[1], op[0]);
  and and_11 (MemRead, op[1], not_20_out);
  and and_12 (and_12_out, not_21_out, not_22_out, op[0], Func[2], Func[1]);
  and and_13 (and_13_out, op[3], not_23_out, op[0]);
  and and_14 (and_14_out, not_25_out, not_26_out);
  and and_15 (and_15_out, op[3], op[1], not_27_out);
  and and_16 (writeDataSrc[1], op[3], op[1], not_28_out);
  and and_17 (and_17_out, not_29_out, op[0], Func[2], Func[1]);
  and and_18 (and_18_out, op[3], op[0]);
  or or_1 (MemToReg, not_30_out, op[2]);
  or or_2 (RegWr, and_2_out, and_3_out, and_4_out, and_5_out, and_6_out, and_7_out);
  or or_3 (Alurc, and_8_out, and_9_out);
  or or_4 (Jump, and_12_out, and_13_out);
  or or_5 (RegDst[0], and_14_out, and_15_out);
  or or_6 (writeDataSrc[0], and_17_out, and_18_out);
endmodule
